# Fritzing sketch Override Port (saved by Fritzing 0.8.7b)
stripboards: 1

parts:
  J1 = male pin header, 4 pins [form="♂ (male)"]
  J2 = male pin header, 4 pins [form="♂ (male)"]
  S1 = Pushbutton [package=THT]
  LED1 = LED - 5mm [color="Red (633nm)" package="5 mm [THT]"]
  R1 = Resistor [tolerance=±5% resistance=220 package=THT]
  R2 = Resistor [tolerance=±5% resistance=220 package=THT]

nets:
  N1: J1.pin1, J2.pin4, S1.leg1, R1.Pin_1
  N2: J1.pin2, R1.Pin_0, R2.Pin_1
  N3: J1.pin3, J2.pin3, S1.leg0
  N4: J1.pin4, J2.pin1, LED1.anode
  N5: J2.pin2, LED1.cathode, R2.Pin_0
